# Fritzing sketch Uebung_104 (saved by Fritzing 1.0.4)
breadboards: 1

parts:
  R1 = Resistor [tolerance=±5% resistance=10k power=0.25W package=THT]
  R2 = Temperature Sensor (Thermistor) [thermistor_type=NTC package=THT]
  Aurix_TC1 = Aurix TC375 Lite Kit

nets:
  N1: R1.Pin_0, R2.pin_1, Aurix_TC1.A5
  N2: R1.Pin_1, Aurix_TC1.5V
  N3: R2.pin_0, Aurix_TC1.GND

notes:
  MCP2515

custom parts:
  Aurix TC375 Lite Kit: The Aurix TC375 Lite Kit is a development board based on the Infineon Aurix TC375 microcontroller. It features a 32-bit TriCore™ architecture with 3 cores operating at up to 300 MHz, 6 MB of flash memory, and 728 KB of RAM. The board is equipped with multiple interfaces, including CAN, UART, SPI, and I²C, as well as a micro-USB connector for programming and power. Additionally, it has an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
