# Fritzing sketch Scheduler2 (saved by Fritzing 1.0.4)
breadboards: 1

parts:
  R2 = Resistor [tolerance=±5% resistance=220 power=0.25W package=THT]
  R4 = Resistor [tolerance=±5% resistance=220 power=0.25W package=THT]
  R5 = Resistor [tolerance=±5% resistance=220 power=0.25W package=THT]
  LED2 = LED - 5mm [color="Red (633nm)" current=0.030A package="5 mm [THT]"]
  LED3 = LED - 5mm [color="Orange (612nm)" current=0.030A package="5 mm [THT]"]
  LED4 = LED - 5mm [color="Green (565nm)" current=0.030A package="5 mm [THT]"]
  S1 = Pushbutton [package="[THT]"]
  R6 = Resistor [tolerance=±5% resistance=10k power=0.25W package=THT]
  Aurix_TC1 = Aurix TC375 Lite Kit

nets:
  N1: R2.Pin_0, Aurix_TC1.P02.6
  N2: R2.Pin_1, LED4.anode
  N3: R4.Pin_0, Aurix_TC1.P10.5
  N4: R4.Pin_1, LED3.anode
  N5: R5.Pin_0, Aurix_TC1.P10.1
  N6: R5.Pin_1, LED2.anode
  N7: LED2.cathode, LED3.cathode, LED4.cathode, S1.Pin_1, S1.Pin_2, Aurix_TC1.GND
  N8: S1.Pin_3, S1.Pin_4, R6.Pin_1, Aurix_TC1.P15.2
  N9: R6.Pin_0, Aurix_TC1.5V

custom parts:
  Aurix TC375 Lite Kit: The Aurix TC375 Lite Kit is a development board based on the Infineon Aurix TC375 microcontroller. It features a 32-bit TriCore™ architecture with 3 cores operating at up to 300 MHz, 6 MB of flash memory, and 728 KB of RAM. The board is equipped with multiple interfaces, including CAN, UART, SPI, and I²C, as well as a micro-USB connector for programming and power. Additionally, it has an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
