# Fritzing sketch TrafficLight (saved by Fritzing 0.9.4)
breadboards: 1

parts:
  R2 = Resistor [tolerance=±5% resistance=220 package=THT]
  R4 = Resistor [tolerance=±5% resistance=220 package=THT]
  LED2 = LED - 5mm [color="Red (633nm)" package="5 mm [THT]"]
  LED3 = LED - 5mm [color="Orange (612nm)" package="5 mm [THT]"]
  S1 = Pushbutton [package="[THT]"]
  R5 = Resistor [tolerance=±5% resistance=220 package=THT]
  R6 = Resistor [tolerance=±5% resistance=220 package=THT]
  LED5 = LED - 5mm [color="Green (565nm)" package="5 mm [THT]"]
  R7 = Resistor [tolerance=±5% resistance=220 package=THT]
  LED6 = LED - 5mm [color="Red (633nm)" package="5 mm [THT]"]
  R8 = Resistor [tolerance=±5% resistance=10k package=THT]
  R9 = Resistor [tolerance=±5% resistance=10k package=THT]
  Bauteil1 = Arduino Uno (Rev3)
  LED7 = LED - 5mm [color="Green (565nm)" package="5 mm [THT]"]
  S2 = Toggle Switch [package=THT]

nets:
  N1: R2.Pin_0, Bauteil1.D8
  N2: R2.Pin_1, LED7.anode
  N3: R4.Pin_0, Bauteil1.D9_PWM
  N4: R4.Pin_1, LED3.anode
  N5: LED2.cathode, LED3.cathode, S1.Pin_1, S1.Pin_2, LED5.cathode, LED6.cathode, Bauteil1.GND, LED7.cathode, S2.COM
  N6: LED2.anode, R6.Pin_1
  N7: S1.Pin_3, S1.Pin_4, R8.Pin_1, Bauteil1.D2
  N8: R5.Pin_0, Bauteil1.D11_PWM/MOSI
  N9: R5.Pin_1, LED5.anode
  N10: R6.Pin_0, Bauteil1.D10_PWM/SS
  N11: R7.Pin_0, Bauteil1.D12/MISO
  N12: R7.Pin_1, LED6.anode
  N13: R8.Pin_0, R9.Pin_0, Bauteil1.5V
  N14: R9.Pin_1, Bauteil1.D1/TX, S2.L1
