# Fritzing sketch TrafficLight (saved by Fritzing 1.0.4)
breadboards: 1

parts:
  R2 = Resistor [tolerance=±5% resistance=220 power=0.25W package=THT]
  R4 = Resistor [tolerance=±5% resistance=220 power=0.25W package=THT]
  LED2 = LED - 5mm [color="Red (633nm)" current=0.030A package="5 mm [THT]"]
  LED3 = LED - 5mm [color="Orange (612nm)" current=0.030A package="5 mm [THT]"]
  S1 = Pushbutton [package="[THT]"]
  R5 = Resistor [tolerance=±5% resistance=220 power=0.25W package=THT]
  R6 = Resistor [tolerance=±5% resistance=220 power=0.25W package=THT]
  LED5 = LED - 5mm [color="Green (565nm)" current=0.030A package="5 mm [THT]"]
  R7 = Resistor [tolerance=±5% resistance=220 power=0.25W package=THT]
  LED6 = LED - 5mm [color="Red (633nm)" current=0.030A package="5 mm [THT]"]
  R8 = Resistor [tolerance=±5% resistance=10k power=0.25W package=THT]
  R9 = Resistor [tolerance=±5% resistance=10k power=0.25W package=THT]
  LED7 = LED - 5mm [color="Green (565nm)" current=0.030A package="5 mm [THT]"]
  S2 = Toggle Switch [package=THT]
  Aurix_TC1 = Aurix TC375 Lite Kit

nets:
  N1: R2.Pin_0, Aurix_TC1.P02.6
  N2: R2.Pin_1, LED7.anode
  N3: R4.Pin_0, Aurix_TC1.P02.7
  N4: R4.Pin_1, LED3.anode
  N5: LED2.cathode, LED3.cathode, S1.Pin_1, S1.Pin_2, LED5.cathode, LED6.cathode, LED7.cathode, S2.COM, Aurix_TC1.GND
  N6: LED2.anode, R6.Pin_1
  N7: S1.Pin_3, S1.Pin_4, R8.Pin_1, Aurix_TC1.P02.0
  N8: R5.Pin_0, Aurix_TC1.P10.3
  N9: R5.Pin_1, LED5.anode
  N10: R6.Pin_0, Aurix_TC1.P10.5
  N11: R7.Pin_0, Aurix_TC1.P10.1
  N12: R7.Pin_1, LED6.anode
  N13: R8.Pin_0, R9.Pin_0, Aurix_TC1.5V
  N14: R9.Pin_1, S2.L1, Aurix_TC1.P15.2

custom parts:
  Aurix TC375 Lite Kit: The Aurix TC375 Lite Kit is a development board based on the Infineon Aurix TC375 microcontroller. It features a 32-bit TriCore™ architecture with 3 cores operating at up to 300 MHz, 6 MB of flash memory, and 728 KB of RAM. The board is equipped with multiple interfaces, including CAN, UART, SPI, and I²C, as well as a micro-USB connector for programming and power. Additionally, it has an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
